# Fritzing sketch humidity circuit (saved by Fritzing 0.9.3b)
breadboards: 1

parts:
  Part1 = Humidity Sensor - HIH-4030 Breakout
  Part2 = Arduino Uno (Rev3)

nets:
  GND: Part1.GND, Part2.GND
  N1: Part1.OUT, Part2.A0
  VCC: Part1.VCC, Part2.3V3
